# Fritzing sketch Prototype-ESP32-FLEX-MPU-MAX (saved by Fritzing 0.9.3b)
perfboards: 2

parts:
  M1 = gy9250
  A7 = Esp32-c3 super mini
  M2 = gy9250
  A8 = Esp32-c3 super mini
  Mod1 = AD8232 HeartRate Monitor [part_number=SEN-12650]
  J1 = female pin header, 1 pin [form="♀ (female)"]
  J2 = female pin header, 1 pin [form="♀ (female)"]
  A9 = Esp32-c3 super mini  # not connected
  M3 = gy9250  # not connected
  Mod2 = AD8232 HeartRate Monitor [part_number=SEN-12650]  # not connected
  Mod3 = AD8232 HeartRate Monitor [part_number=SEN-12650]  # not connected
  M4 = gy9250  # not connected
  A10 = Esp32-c3 super mini  # not connected

nets:
  N1: M1.pin1, A7.Pin_14
  N2: M1.pin2, A7.Pin_15
  N3: M1.pin3, A7.Pin_9
  N4: M1.pin4, A7.Pin_10
  N5: M2.pin1, A8.Pin_14, Mod1.GND, J2.pin1
  N6: M2.pin2, A8.Pin_15, Mod1.3.3v, J1.pin1
  N7: M2.pin3, A8.Pin_9
  N8: M2.pin4, A8.Pin_10
  N9: A8.Pin_1, Mod1.LO-
  N10: A8.Pin_11, Mod1.OUTPUT
  N11: A8.Pin_12, Mod1.LO+

custom parts:
  gy9250: MPU-9250 module (three-axis gyroscope + three-axis acceleration + three-axis magnetic field). The generic model from ebay et. al. rather than the Sparkfun version.
  Esp32-c3 super mini: ESP32-C3 Development Board ESP32 SuperMini Development Board ESP32 Development Board WiFi Bluetooth.
  AD8232 HeartRate Monitor: Sparkfun single lead heart rate monitor - Ad8232.
